// Logisim project MIPS_Single.circ as structural Verilog: 10 circuits, main circuit MIPS_Single_Top
module ALU (
  input  [31:0] ALUA,
  input  [31:0] ALUB,
  input  [3:0] ALUSel,
  output [31:0] ALURESULT
);

  wire comparator_1_lt, XOR_2_out;
  wire [31:0] adder_1_out, adder_2_out, AND_out, bit_extender_1_out, bit_extender_2_out, multiplexer_1_out,
       multiplexer_2_out, not_1_out, not_2_out, not_3_out, OR_out, shifter_1_out, shifter_2_out,
       shifter_3_out, XOR_out;

  assign not_1_out = ~ALUB;  // NOT_Gate not_1, 32 bits wide
  assign not_2_out = ~ALUA;  // NOT_Gate not_2, 32 bits wide
  Multiplexer #(.width(32)) multiplexer_1 (
    .in0(ALUB), .in1(not_1_out), .out(multiplexer_1_out), .sel(ALUSel[0]), .en(1'b1));
  Adder #(.width(32)) adder_1 (.a(ALUA), .b(multiplexer_1_out), .out(adder_1_out), .cin(ALUSel[0]));  // open: cout
  assign AND_out = ALUA & ALUB;  // AND_Gate AND, 32 bits wide
  assign OR_out = ALUA | ALUB;  // OR_Gate OR, 32 bits wide
  assign XOR_out = ALUA ^ ALUB;  // XOR_Gate XOR, 32 bits wide
  xor XOR_2 (XOR_2_out, ALUA[31], ALUB[31]);
  Comparator #(.width(32), .mode("unsigned")) comparator_1 (.a(ALUA), .b(ALUB), .lt(comparator_1_lt));  // open: gt, eq
  Shifter #(.width(32)) shifter_1 (.in(ALUA), .\dist (ALUB[4:0]), .out(shifter_1_out));
  Shifter #(.width(32), .shift("lr")) shifter_2 (.in(ALUA), .\dist (ALUB[4:0]), .out(shifter_2_out));
  Shifter #(.width(32), .shift("ar")) shifter_3 (.in(ALUA), .\dist (ALUB[4:0]), .out(shifter_3_out));
  Adder #(.width(32)) adder_2 (.a(32'h1), .b(not_2_out), .out(adder_2_out));  // open: cin, cout
  assign bit_extender_1_out = {{31{1'b0}}, ALUA[31]};  // Bit_Extender bit_extender_1
  assign bit_extender_2_out = {{31{1'b0}}, comparator_1_lt};  // Bit_Extender bit_extender_2
  Multiplexer #(.width(32)) multiplexer_2 (
    .in0(bit_extender_2_out), .in1(bit_extender_1_out), .out(multiplexer_2_out), .sel(XOR_2_out), .en(1'b1));
  assign not_3_out = ~OR_out;  // NOT_Gate not_3, 32 bits wide
  Multiplexer #(.select(4), .width(32)) multiplexer_3 (
    .in0(adder_1_out), .in1(adder_1_out), .in2(AND_out), .in3(OR_out), .in4(XOR_out),
    .in5(multiplexer_2_out), .in6(bit_extender_2_out), .in7(shifter_1_out), .in8(shifter_2_out),
    .in9(shifter_3_out), .in10(not_3_out), .in11(adder_2_out), .in15({32{1'b0}}), .out(ALURESULT),
    .sel(ALUSel), .en(1'b1));  // open: in12, in13, in14

  // Notes on the sheet:
  //   if SUB
  //   Adder
  //   A[31] != B[31]
  //   Unsigned Comp
  //   Left Shifter
  //   Logical RIght Shifter
  //   Arithmetic RIght Shifter
  //   ABS
endmodule

module Branch_Comp (
  input  [31:0] Data_rs,
  input  [31:0] Data_rt,
  input  BrSel,
  output BranchTaken
);

  wire comparator_1_eq, not_1_out;

  Comparator #(.width(32)) comparator_1 (.a(Data_rs), .b(Data_rt), .eq(comparator_1_eq));  // open: gt, lt
  not not_1 (not_1_out, comparator_1_eq);
  Multiplexer multiplexer_1 (.in0(comparator_1_eq), .in1(not_1_out), .out(BranchTaken), .sel(BrSel), .en(1'b1));
endmodule

module immediate_generator (
  input  [15:0] imm16,
  input  [1:0] ImmSel,
  output [31:0] ImmVal
);

  wire [31:0] bit_extender_1_out, bit_extender_2_out, shifter_1_out;

  assign bit_extender_1_out = {{16{imm16[15]}}, imm16};  // Bit_Extender bit_extender_1
  assign bit_extender_2_out = {{16{1'b0}}, imm16};  // Bit_Extender bit_extender_2
  Shifter #(.width(32)) shifter_1 (.in(bit_extender_1_out), .\dist (5'b00010), .out(shifter_1_out));
  Multiplexer #(.select(2), .width(32)) multiplexer_1 (
    .in0(bit_extender_1_out), .in1(bit_extender_2_out), .in2({imm16, {16{1'b0}}}), .in3(shifter_1_out),
    .out(ImmVal), .sel(ImmSel), .en(1'b1));
endmodule

module instruction_splitter (
  input  [31:0] Inst,
  output [4:0] rs,
  output [4:0] rt,
  output [4:0] rd,
  output [15:0] imm16,
  output [25:0] target26,
  output [4:0] shamt,
  output [5:0] opcode,
  output [5:0] funct
);


  assign funct = Inst[5:0];
  assign imm16 = Inst[15:0];
  assign opcode = Inst[31:26];
  assign rd = Inst[15:11];
  assign rs = Inst[25:21];
  assign rt = Inst[20:16];
  assign shamt = Inst[10:6];
  assign target26 = Inst[25:0];
endmodule

module Jump_target_generator (
  input  [25:0] target26,
  input  [31:0] PCPlus4,
  output [31:0] JumpImmTarget
);


  assign JumpImmTarget = {PCPlus4[31:28], target26, 2'b00};
endmodule

module pc_control (
  input  Jump,
  input  Branch,
  input  BranchTaken,
  output [1:0] out_4
);

  wire and_1_out;
  wire [1:0] multiplexer_1_out;

  and and_1 (and_1_out, Branch, BranchTaken);
  Multiplexer #(.width(2), .enable("false")) multiplexer_1 (
    .in0(2'b00), .in1(2'b01), .out(multiplexer_1_out), .sel(and_1_out));
  Multiplexer #(.width(2), .enable("false")) multiplexer_2 (
    .in0(multiplexer_1_out), .in1(2'b10), .out(out_4), .sel(Jump));
endmodule

module Control_Unit (
  input  [5:0] opcode,
  input  [5:0] funct,
  output JumpSel,
  output Jump,
  output Branch,
  output LoadEx,
  output [1:0] MemRW,
  output [1:0] WdLen,
  output [1:0] WBSel,
  output [3:0] ALUSel,
  output BrSel,
  output [1:0] ImmSel,
  output [2:0] BSel,
  output [1:0] ASel,
  output [1:0] DestSel,
  output RegWEn
);

  wire [31:0] rom_1_data;

  ROM #(.addrWidth(12), .dataWidth(32)) rom_1 (
    .addr({opcode, funct}),
    .data({rom_1_data[31:27], RegWEn, DestSel, ASel, BSel, ImmSel, BrSel, ALUSel, WBSel, WdLen, rom_1_data[7], MemRW, LoadEx, Branch, Jump, JumpSel, rom_1_data[0]}));  // open: sel

  // Notes on the sheet:
  //   contents of rom_1 (hex, n*v repeats v):
  //   5d07700 3a0ff00 5d08700 5d09700 5d87700 3a0ff00 5d88700 5d89700 338ff06 538fb06 22*3a0ff00 5000700
  //   5000700 5001700 5001700 5002700 5003700 5004700 500a700 3a0ff00 3a0ff00 5005700 5006700 520b700
  //   83*3a0ff00 64*3b8ff04 64*6b8fb04 64*34e0f08 64*34f0f08 128*3a0ff00 128*4080700 64*4085700 64*4086700
  //   64*40a2700 64*40a3700 64*40a4700 64*48c0700 1024*3a0ff00 64*4080020 64*4080120 64*3a0ff00 64*4080220
  //   64*4080030 64*4080130 128*3a0ff00 64*3080c40 64*3080d40 64*3a0ff00 64*3080e40 1280*3a0ff00
endmodule

module Data_memory (
  input  [31:0] Addr,
  input  [31:0] Data_rt,
  input  clk,
  input  LoadEx,
  input  [1:0] MemRW,
  input  [1:0] WdLen,
  output [31:0] Data_RD,
  output MisalignedAccessFlag
);

  wire and_1_out, and_2_out, \byte , half, load, none, not_1_out, not_2_out, not_3_out, not_4_out, or_1_out,
       or_2_out, or_3_out, RAM_load_en, RAM_store_en, store, word;
  wire [7:0] multiplexer_4_out;
  wire [15:0] multiplexer_5_out;
  wire [31:0] bit_extender_1_out, bit_extender_2_out, bit_extender_3_out, bit_extender_4_out,
       multiplexer_1_out, multiplexer_2_out, multiplexer_3_out, multiplexer_6_out, multiplexer_7_out,
       multiplexer_8_out, ReadWord;

  // Probe on Data_rt
  Multiplexer #(.select(2), .width(32)) multiplexer_1 (
    .in0({ReadWord[31:8], Data_rt[7:0]}), .in1({ReadWord[31:16], Data_rt[7:0], ReadWord[7:0]}),
    .in2({ReadWord[31:24], Data_rt[7:0], ReadWord[15:0]}), .in3({Data_rt[7:0], ReadWord[23:0]}),
    .out(multiplexer_1_out), .sel(Addr[1:0]), .en(1'b1));
  Multiplexer #(.width(32)) multiplexer_2 (
    .in0({ReadWord[31:16], Data_rt[15:0]}), .in1({Data_rt[15:0], ReadWord[15:0]}), .out(multiplexer_2_out),
    .sel(Addr[1]), .en(1'b1));
  Multiplexer #(.select(2), .width(32)) multiplexer_3 (
    .in0(multiplexer_1_out), .in1(multiplexer_2_out), .in2(Data_rt), .in3({32{1'b0}}),
    .out(multiplexer_3_out), .sel(WdLen), .en(1'b1));
  RAM #(.addrWidth(10), .dataWidth(32), .bus("separate")) ram_1 (
    .addr({Addr[9:2], 2'b00}), .din(multiplexer_3_out), .data(ReadWord), .str(RAM_store_en), .clk(clk),
    .ld(1'b1));  // open: sel, clr
  Multiplexer #(.select(2), .width(8)) multiplexer_4 (
    .in0(ReadWord[7:0]), .in1(ReadWord[15:8]), .in2(ReadWord[23:16]), .in3(ReadWord[31:24]),
    .out(multiplexer_4_out), .sel(Addr[1:0]), .en(1'b1));
  Multiplexer #(.width(16)) multiplexer_5 (
    .in0(ReadWord[15:0]), .in1(ReadWord[31:16]), .out(multiplexer_5_out), .sel(Addr[1]), .en(1'b1));
  Comparator #(.width(2)) comparator_1 (.a(MemRW), .b(2'b10), .eq(store));  // open: gt, lt
  Comparator #(.width(2)) comparator_2 (.a(MemRW), .b(2'b01), .eq(load));  // open: gt, lt
  Comparator #(.width(2)) comparator_3 (.a(WdLen), .b(2'b00), .eq(\byte ));  // open: gt, lt
  Comparator #(.width(2)) comparator_4 (.a(WdLen), .b(2'b01), .eq(half));  // open: gt, lt
  Comparator #(.width(2)) comparator_5 (.a(WdLen), .b(2'b10), .eq(word));  // open: gt, lt
  Comparator #(.width(2)) comparator_6 (.a(WdLen), .b(2'b11), .eq(none));  // open: gt, lt
  assign bit_extender_1_out = {{24{multiplexer_4_out[7]}}, multiplexer_4_out};  // Bit_Extender bit_extender_1
  Multiplexer #(.width(32)) multiplexer_6 (
    .in0(bit_extender_1_out), .in1(bit_extender_2_out), .out(multiplexer_6_out), .sel(LoadEx), .en(1'b1));
  assign bit_extender_2_out = {{24{1'b0}}, multiplexer_4_out};  // Bit_Extender bit_extender_2
  assign bit_extender_3_out = {{16{multiplexer_5_out[15]}}, multiplexer_5_out};  // Bit_Extender bit_extender_3
  Multiplexer #(.width(32)) multiplexer_7 (
    .in0(bit_extender_3_out), .in1(bit_extender_4_out), .out(multiplexer_7_out), .sel(LoadEx), .en(1'b1));
  assign bit_extender_4_out = {{16{1'b0}}, multiplexer_5_out};  // Bit_Extender bit_extender_4
  or or_1 (or_1_out, Addr[0], Addr[1]);
  Multiplexer #(.select(2), .width(32)) multiplexer_8 (
    .in0(multiplexer_6_out), .in1(multiplexer_7_out), .in2(ReadWord), .in3({32{1'b0}}),
    .out(multiplexer_8_out), .sel(WdLen), .en(1'b1));
  and and_1 (and_1_out, or_1_out, word);
  and and_2 (and_2_out, Addr[0], half);
  not not_1 (not_1_out, MisalignedAccessFlag);
  and and_3 (RAM_load_en, not_1_out, not_2_out, load);
  not not_2 (not_2_out, none);
  not not_3 (not_3_out, MisalignedAccessFlag);
  not not_4 (not_4_out, none);
  and and_4 (RAM_store_en, not_3_out, not_4_out, store);
  or or_2 (or_2_out, and_1_out, and_2_out);
  or or_3 (or_3_out, load, store);
  Multiplexer #(.width(32)) multiplexer_9 (
    .in0({32{1'b0}}), .in1(multiplexer_8_out), .out(Data_RD), .sel(RAM_load_en), .en(1'b1));
  and and_5 (MisalignedAccessFlag, or_2_out, or_3_out);
  // Probe on Data_RD

  // Other names for the same wires on the sheet: Data_rt_7_0[7:0] = Data_rt[7:0]; Data_rt_15_0[15:0] = Data_rt[15:0];
  //   ReadWord_15_0[15:0] = ReadWord[15:0]; ReadWord_23_0[23:0] = ReadWord[23:0];
  //   ReadWord_31_8[23:0] = ReadWord[31:8]; ReadWord_31_16[15:0] = ReadWord[31:16];
  //   ReadWord_31_24[7:0] = ReadWord[31:24]; ReadWord_7_0[7:0] = ReadWord[7:0]; lane[1:0] = Addr[1:0];
  //   lane_0 = Addr[0]; lane_1 = Addr[1]
endmodule

module MIPS_Single_Top (
);

  wire branch_comp_1_branchtaken, CLK, control_unit_1_branch, control_unit_1_brsel, control_unit_1_jump,
       control_unit_1_jumpsel, control_unit_1_loadex, control_unit_1_regwen;
  wire [1:0] control_unit_1_asel, control_unit_1_destsel, control_unit_1_immsel, control_unit_1_memrw,
       control_unit_1_wbsel, control_unit_1_wdlen, pc_control_1_out_4;
  wire [2:0] control_unit_1_bsel;
  wire [3:0] control_unit_1_alusel;
  wire [4:0] instruction_splitter_1_rd, instruction_splitter_1_rs, instruction_splitter_1_rt,
       instruction_splitter_1_shamt, multiplexer_3_out;
  wire [5:0] instruction_splitter_1_funct, instruction_splitter_1_opcode;
  wire [15:0] instruction_splitter_1_imm16;
  wire [25:0] instruction_splitter_1_target26;
  wire [31:0] adder_1_out, alu_1_aluresult, data_memory_1_data_rd, immediate_generator_1_immval,
       jump_target_generator_1_jumpimmtarget, multiplexer_1_out, multiplexer_2_out, multiplexer_4_out,
       multiplexer_5_out, multiplexer_6_out, PC_q, reg_file_1__30, reg_file_1_data_rs, reg_file_1_data_rt,
       rom_1_data;

  Multiplexer #(.select(2), .width(32)) multiplexer_1 (
    .in0(adder_1_out), .in1(alu_1_aluresult), .in2(multiplexer_2_out), .out(multiplexer_1_out),
    .sel(pc_control_1_out_4));  // open: in3, en
  Register #(.width(32)) PC (.D(multiplexer_1_out), .Q(PC_q), .clk(CLK));  // open: en, clr
  Clock clock_1 (.out(CLK));
  Adder #(.width(32)) adder_1 (.a(32'h4), .b(PC_q), .out(adder_1_out));  // open: cin, cout
  Jump_target_generator jump_target_generator_1 (
    .target26(instruction_splitter_1_target26), .PCPlus4(adder_1_out),
    .JumpImmTarget(jump_target_generator_1_jumpimmtarget));
  ROM #(.addrWidth(24), .dataWidth(32)) rom_1 (.addr(PC_q[25:2]), .data(rom_1_data));  // open: sel
  instruction_splitter instruction_splitter_1 (
    .Inst(rom_1_data), .opcode(instruction_splitter_1_opcode), .rs(instruction_splitter_1_rs),
    .rt(instruction_splitter_1_rt), .rd(instruction_splitter_1_rd), .shamt(instruction_splitter_1_shamt),
    .funct(instruction_splitter_1_funct), .imm16(instruction_splitter_1_imm16),
    .target26(instruction_splitter_1_target26));
  Multiplexer #(.width(32)) multiplexer_2 (
    .in0(jump_target_generator_1_jumpimmtarget), .in1(reg_file_1_data_rs), .out(multiplexer_2_out),
    .sel(control_unit_1_jumpsel));  // open: en
  Reg_file reg_file_1 (
    .Data_WR(multiplexer_6_out), .Addr_rs(instruction_splitter_1_rs), .Addr_rt(instruction_splitter_1_rt),
    .Addr_WR(multiplexer_3_out), .Data_rs(reg_file_1_data_rs), .Data_rt(reg_file_1_data_rt), .CLK(CLK),
    .RegWEn(control_unit_1_regwen), ._30(reg_file_1__30));  // open: RESET
  // Probe on reg_file_1__30
  Multiplexer #(.select(2), .width(5)) multiplexer_3 (
    .in0(instruction_splitter_1_rt), .in1(instruction_splitter_1_rd), .in2({5{1'b1}}), .in3({5{1'b0}}),
    .out(multiplexer_3_out), .sel(control_unit_1_destsel));  // open: en
  immediate_generator immediate_generator_1 (
    .imm16(instruction_splitter_1_imm16), .ImmSel(control_unit_1_immsel),
    .ImmVal(immediate_generator_1_immval));
  Control_Unit control_unit_1 (
    .opcode(instruction_splitter_1_opcode), .funct(instruction_splitter_1_funct), .Jump(control_unit_1_jump),
    .Branch(control_unit_1_branch), .LoadEx(control_unit_1_loadex), .MemRW(control_unit_1_memrw),
    .WdLen(control_unit_1_wdlen), .WBSel(control_unit_1_wbsel), .ALUSel(control_unit_1_alusel),
    .BrSel(control_unit_1_brsel), .ImmSel(control_unit_1_immsel), .BSel(control_unit_1_bsel),
    .ASel(control_unit_1_asel), .DestSel(control_unit_1_destsel), .RegWEn(control_unit_1_regwen),
    .JumpSel(control_unit_1_jumpsel));
  Multiplexer #(.select(3), .width(32)) multiplexer_4 (
    .in0(reg_file_1_data_rt), .in1(immediate_generator_1_immval),
    .in2({{27{1'b0}}, instruction_splitter_1_shamt}), .in3(reg_file_1_data_rs), .in4({32{1'b0}}),
    .out(multiplexer_4_out), .sel(control_unit_1_bsel));  // open: in5, in6, in7, en
  Branch_Comp branch_comp_1 (
    .Data_rs(reg_file_1_data_rs), .Data_rt(reg_file_1_data_rt), .BrSel(control_unit_1_brsel),
    .BranchTaken(branch_comp_1_branchtaken));
  pc_control pc_control_1 (
    .Jump(control_unit_1_jump), .Branch(control_unit_1_branch), .BranchTaken(branch_comp_1_branchtaken),
    .out_4(pc_control_1_out_4));
  Multiplexer #(.select(2), .width(32)) multiplexer_5 (
    .in0(reg_file_1_data_rs), .in1(adder_1_out), .in2({32{1'b0}}), .in3(reg_file_1_data_rt),
    .out(multiplexer_5_out), .sel(control_unit_1_asel));  // open: en
  ALU alu_1 (
    .ALUA(multiplexer_5_out), .ALUB(multiplexer_4_out), .ALUSel(control_unit_1_alusel),
    .ALURESULT(alu_1_aluresult));
  Data_memory data_memory_1 (
    .Addr(alu_1_aluresult), .Data_rt(reg_file_1_data_rt), .LoadEx(control_unit_1_loadex),
    .MemRW(control_unit_1_memrw), .WdLen(control_unit_1_wdlen), .Data_RD(data_memory_1_data_rd), .clk(CLK));  // open: MisalignedAccessFlag
  Multiplexer #(.select(2), .width(32)) multiplexer_6 (
    .in0(data_memory_1_data_rd), .in1(alu_1_aluresult), .in2(adder_1_out), .out(multiplexer_6_out),
    .sel(control_unit_1_wbsel));  // open: in3, en

  // Notes on the sheet:
  //   contents of rom_1 (hex, n*v repeats v):
  //   201e0000 3c011234 34215678 2002fffb 2403000a 632020 832821 a33022 653823 254024 1034825 1255026
  //   1405827 43602a 43682b 40702c e7880 f8042 28843 20120003 24e9804 253a006 242a807 303600ff 3ad700f0
  //   28580000 2c590001 ac010000 8c1a0000 801b0000 901c0001 841d0000 a0030001 90050001 a40e0002 94060002
  //   8c070000 10a30001 200d0bad 14c30001 20190bad 8000030 200d0bad 20090033 3e05809 200c0044 8000034
  //   20190bad c00002b 23180001 1600008 20190bad 1f021 3c2f021 3c3f021 3c4f021 3c5f021 3c6f021 3c7f021
  //   3c8f021 3c9f021 3caf021 3ccf021 3cdf021 3cef021 3cff021 3d0f021 3d1f021 3d2f021 3d3f021 3d4f021
  //   3d5f021 3d6f021 3d7f021 3d8f021 3d9f021 3daf021 3dbf021 3dcf021 3ddf021 8000050
endmodule

module Reg_file (
  input  CLK,
  input  RESET,
  input  [31:0] Data_WR,
  input  [4:0] Addr_rs,
  input  [4:0] Addr_rt,
  input  [4:0] Addr_WR,
  input  RegWEn,
  output [31:0] Data_rs,
  output [31:0] Data_rt,
  output [31:0] _30
);

  wire EN__1, EN__2, EN__3, EN__4, EN__5, EN__6, EN__7, EN__8, EN__9, EN__10, EN__11, EN__12, EN__13, EN__14,
       EN__15, EN__16, EN__17, EN__18, EN__19, EN__20, EN__21, EN__22, EN__23, EN__24, EN__25, EN__26,
       EN__27, EN__28, EN__29, EN__30, EN__31;
  wire [4:0] multiplexer_1_out;
  wire [31:0] Q__1, Q__2, Q__3, Q__4, Q__5, Q__6, Q__7, Q__8, Q__9, Q__10, Q__11, Q__12, Q__13, Q__14, Q__15,
       Q__16, Q__17, Q__18, Q__19, Q__20, Q__21, Q__22, Q__23, Q__24, Q__25, Q__26, Q__27, Q__28, Q__29,
       Q__31;

  Decoder #(.select(5)) decoder_1 (
    .out1(EN__1), .out2(EN__2), .out3(EN__3), .out4(EN__4), .out5(EN__5), .out6(EN__6), .out7(EN__7),
    .out8(EN__8), .out9(EN__9), .out10(EN__10), .out11(EN__11), .out12(EN__12), .out13(EN__13),
    .out14(EN__14), .out15(EN__15), .out16(EN__16), .out17(EN__17), .out18(EN__18), .out19(EN__19),
    .out20(EN__20), .out21(EN__21), .out22(EN__22), .out23(EN__23), .out24(EN__24), .out25(EN__25),
    .out26(EN__26), .out27(EN__27), .out28(EN__28), .out29(EN__29), .out30(EN__30), .out31(EN__31),
    .sel(multiplexer_1_out), .en(1'b1));  // open: out0
  Multiplexer #(.width(5)) multiplexer_1 (
    .in0({5{1'b0}}), .in1(Addr_WR), .out(multiplexer_1_out), .sel(RegWEn), .en(1'b1));
  Register #(.width(32)) register_1 (.D(Data_WR), .en(EN__1), .Q(Q__1), .clk(CLK), .clr(RESET));
  Register #(.width(32)) register_2 (.D(Data_WR), .en(EN__2), .Q(Q__2), .clk(CLK), .clr(RESET));
  Register #(.width(32)) register_3 (.D(Data_WR), .en(EN__3), .Q(Q__3), .clk(CLK), .clr(RESET));
  Register #(.width(32)) register_4 (.D(Data_WR), .en(EN__4), .Q(Q__4), .clk(CLK), .clr(RESET));
  Register #(.width(32)) register_5 (.D(Data_WR), .en(EN__5), .Q(Q__5), .clk(CLK), .clr(RESET));
  Register #(.width(32)) register_6 (.D(Data_WR), .en(EN__6), .Q(Q__6), .clk(CLK), .clr(RESET));
  Register #(.width(32)) register_7 (.D(Data_WR), .en(EN__7), .Q(Q__7), .clk(CLK), .clr(RESET));
  Register #(.width(32)) register_8 (.D(Data_WR), .en(EN__8), .Q(Q__8), .clk(CLK), .clr(RESET));
  Register #(.width(32)) register_9 (.D(Data_WR), .en(EN__9), .Q(Q__9), .clk(CLK), .clr(RESET));
  Register #(.width(32)) register_10 (.D(Data_WR), .en(EN__10), .Q(Q__10), .clk(CLK), .clr(RESET));
  Register #(.width(32)) register_11 (.D(Data_WR), .en(EN__11), .Q(Q__11), .clk(CLK), .clr(RESET));
  Register #(.width(32)) register_12 (.D(Data_WR), .en(EN__12), .Q(Q__12), .clk(CLK), .clr(RESET));
  Register #(.width(32)) register_13 (.D(Data_WR), .en(EN__13), .Q(Q__13), .clk(CLK), .clr(RESET));
  Register #(.width(32)) register_14 (.D(Data_WR), .en(EN__14), .Q(Q__14), .clk(CLK), .clr(RESET));
  Register #(.width(32)) register_15 (.D(Data_WR), .en(EN__15), .Q(Q__15), .clk(CLK), .clr(RESET));
  Register #(.width(32)) register_16 (.D(Data_WR), .en(EN__16), .Q(Q__16), .clk(CLK), .clr(RESET));
  Register #(.width(32)) register_17 (.D(Data_WR), .en(EN__17), .Q(Q__17), .clk(CLK), .clr(RESET));
  Register #(.width(32)) register_18 (.D(Data_WR), .en(EN__18), .Q(Q__18), .clk(CLK), .clr(RESET));
  Register #(.width(32)) register_19 (.D(Data_WR), .en(EN__19), .Q(Q__19), .clk(CLK), .clr(RESET));
  Register #(.width(32)) register_20 (.D(Data_WR), .en(EN__20), .Q(Q__20), .clk(CLK), .clr(RESET));
  Register #(.width(32)) register_21 (.D(Data_WR), .en(EN__21), .Q(Q__21), .clk(CLK), .clr(RESET));
  Register #(.width(32)) register_22 (.D(Data_WR), .en(EN__22), .Q(Q__22), .clk(CLK), .clr(RESET));
  Register #(.width(32)) register_23 (.D(Data_WR), .en(EN__23), .Q(Q__23), .clk(CLK), .clr(RESET));
  Register #(.width(32)) register_24 (.D(Data_WR), .en(EN__24), .Q(Q__24), .clk(CLK), .clr(RESET));
  Register #(.width(32)) register_25 (.D(Data_WR), .en(EN__25), .Q(Q__25), .clk(CLK), .clr(RESET));
  Register #(.width(32)) register_26 (.D(Data_WR), .en(EN__26), .Q(Q__26), .clk(CLK), .clr(RESET));
  Register #(.width(32)) register_27 (.D(Data_WR), .en(EN__27), .Q(Q__27), .clk(CLK), .clr(RESET));
  Register #(.width(32)) register_28 (.D(Data_WR), .en(EN__28), .Q(Q__28), .clk(CLK), .clr(RESET));
  Register #(.width(32)) register_29 (.D(Data_WR), .en(EN__29), .Q(Q__29), .clk(CLK), .clr(RESET));
  Register #(.width(32)) register_30 (.D(Data_WR), .en(EN__30), .Q(_30), .clk(CLK), .clr(RESET));
  Register #(.width(32)) register_31 (.D(Data_WR), .en(EN__31), .Q(Q__31), .clk(CLK), .clr(RESET));
  Multiplexer #(.select(5), .width(32)) multiplexer_2 (
    .in0({32{1'b0}}), .in1(Q__1), .in2(Q__2), .in3(Q__3), .in4(Q__4), .in5(Q__5), .in6(Q__6), .in7(Q__7),
    .in8(Q__8), .in9(Q__9), .in10(Q__10), .in11(Q__11), .in12(Q__12), .in13(Q__13), .in14(Q__14),
    .in15(Q__15), .in16(Q__16), .in17(Q__17), .in18(Q__18), .in19(Q__19), .in20(Q__20), .in21(Q__21),
    .in22(Q__22), .in23(Q__23), .in24(Q__24), .in25(Q__25), .in26(Q__26), .in27(Q__27), .in28(Q__28),
    .in29(Q__29), .in30(_30), .in31(Q__31), .out(Data_rs), .sel(Addr_rs), .en(1'b1));
  Multiplexer #(.select(5), .width(32)) multiplexer_3 (
    .in0({32{1'b0}}), .in1(Q__1), .in2(Q__2), .in3(Q__3), .in4(Q__4), .in5(Q__5), .in6(Q__6), .in7(Q__7),
    .in8(Q__8), .in9(Q__9), .in10(Q__10), .in11(Q__11), .in12(Q__12), .in13(Q__13), .in14(Q__14),
    .in15(Q__15), .in16(Q__16), .in17(Q__17), .in18(Q__18), .in19(Q__19), .in20(Q__20), .in21(Q__21),
    .in22(Q__22), .in23(Q__23), .in24(Q__24), .in25(Q__25), .in26(Q__26), .in27(Q__27), .in28(Q__28),
    .in29(Q__29), .in30(_30), .in31(Q__31), .out(Data_rt), .sel(Addr_rt), .en(1'b1));

  // Other names for the same wires on the sheet: Q__30[31:0] = _30; RST = RESET; WD[31:0] = Data_WR
endmodule
