// Logisim project ALU.circ as structural Verilog: 2 circuits, main circuit ALU_TEST
module ALU (
  input  [31:0] ALU_A,
  input  [31:0] ALU_B,
  input  [3:0] ALUSel,
  output [31:0] ALU_RESULT
);

  wire comparator_1_lt, XOR_2_out;
  wire [31:0] adder_1_out, AND_out, bit_extender_1_out, bit_extender_2_out, multiplexer_1_out,
       multiplexer_2_out, not_1_out, not_2_out, OR_out, shifter_1_out, shifter_2_out, shifter_3_out, XOR_out;

  assign not_1_out = ~ALU_B;  // NOT_Gate not_1, 32 bits wide
  Multiplexer #(.width(32)) multiplexer_1 (
    .in0(ALU_B), .in1(not_1_out), .out(multiplexer_1_out), .sel(ALUSel[0]), .en(1'b1));
  Adder #(.width(32)) adder_1 (.a(ALU_A), .b(multiplexer_1_out), .out(adder_1_out), .cin(ALUSel[0]));  // open: cout
  assign AND_out = ALU_A & ALU_B;  // AND_Gate AND, 32 bits wide
  assign OR_out = ALU_A | ALU_B;  // OR_Gate OR, 32 bits wide
  assign XOR_out = ALU_A ^ ALU_B;  // XOR_Gate XOR, 32 bits wide
  xor XOR_2 (XOR_2_out, ALU_A[31], ALU_B[31]);
  Comparator #(.width(32), .mode("unsigned")) comparator_1 (
    .a(ALU_A), .b(ALU_B), .lt(comparator_1_lt));  // open: gt, eq
  Shifter #(.width(32)) shifter_1 (.in(ALU_A), .\dist (ALU_B[4:0]), .out(shifter_1_out));
  Shifter #(.width(32), .shift("lr")) shifter_2 (.in(ALU_A), .\dist (ALU_B[4:0]), .out(shifter_2_out));
  Shifter #(.width(32), .shift("ar")) shifter_3 (.in(ALU_A), .\dist (ALU_B[4:0]), .out(shifter_3_out));
  assign bit_extender_1_out = {{31{1'b0}}, ALU_A[31]};  // Bit_Extender bit_extender_1
  assign bit_extender_2_out = {{31{1'b0}}, comparator_1_lt};  // Bit_Extender bit_extender_2
  Multiplexer #(.width(32)) multiplexer_2 (
    .in0(bit_extender_2_out), .in1(bit_extender_1_out), .out(multiplexer_2_out), .sel(XOR_2_out), .en(1'b1));
  assign not_2_out = ~OR_out;  // NOT_Gate not_2, 32 bits wide
  Multiplexer #(.select(4), .width(32)) multiplexer_3 (
    .in0(adder_1_out), .in1(adder_1_out), .in2(AND_out), .in3(OR_out), .in4(XOR_out),
    .in5(multiplexer_2_out), .in6(bit_extender_2_out), .in7(shifter_1_out), .in8(shifter_2_out),
    .in9(shifter_3_out), .in10(not_2_out), .in15({32{1'b0}}), .out(ALU_RESULT), .sel(ALUSel), .en(1'b1));  // open: in11, in12, in13, in14

  // Notes on the sheet:
  //   if SUB
  //   Adder
  //   A[31] != B[31]
  //   Unsigned Comp
  //   Left Shifter
  //   Logical RIght Shifter
  //   Arithmetic RIght Shifter
endmodule

module ALU_TEST (
);

  wire clock_1_out, comparator_1_eq, not_1_out;
  wire [3:0] counter_2_q, rom_3_data;
  wire [4:0] counter_1_q;
  wire [31:0] alu_1_alu_result, rom_1_data, rom_2_data, rom_4_data;

  Counter #(.width(5), .max('h15), .ongoal("stay")) counter_1 (
    .Q(counter_1_q), .clk(clock_1_out));  // open: load, D, count, carry, clr
  Clock clock_1 (.out(clock_1_out));
  ROM #(.addrWidth(5), .dataWidth(32)) rom_1 (.addr(counter_1_q), .data(rom_1_data));  // open: sel
  ROM #(.addrWidth(5), .dataWidth(32)) rom_2 (.addr(counter_1_q), .data(rom_2_data));  // open: sel
  ROM #(.addrWidth(5), .dataWidth(4)) rom_3 (.addr(counter_1_q), .data(rom_3_data));  // open: sel
  ROM #(.addrWidth(5), .dataWidth(32)) rom_4 (.addr(counter_1_q), .data(rom_4_data));  // open: sel
  ALU alu_1 (.ALU_A(rom_1_data), .ALU_B(rom_2_data), .ALUSel(rom_3_data), .ALU_RESULT(alu_1_alu_result));
  Hex_Digit_Display hex_digit_display_1 (.value(alu_1_alu_result[31:28]), .dp(1'b1));
  Comparator #(.width(32)) comparator_1 (.a(alu_1_alu_result), .b(rom_4_data), .eq(comparator_1_eq));  // open: gt, lt
  Hex_Digit_Display hex_digit_display_2 (.value(alu_1_alu_result[23:20]), .dp(1'b1));
  Hex_Digit_Display hex_digit_display_3 (.value(alu_1_alu_result[27:24]), .dp(1'b1));
  not not_1 (not_1_out, comparator_1_eq);
  Hex_Digit_Display hex_digit_display_4 (.value(alu_1_alu_result[19:16]), .dp(1'b1));
  Counter #(.width(4), .max('h5)) counter_2 (
    .count(not_1_out), .Q(counter_2_q), .clk(clock_1_out));  // open: load, D, carry, clr
  Hex_Digit_Display hex_digit_display_5 (.value(alu_1_alu_result[11:8]), .dp(1'b1));
  Hex_Digit_Display hex_digit_display_6 (.value(alu_1_alu_result[15:12]), .dp(1'b1));
  Hex_Digit_Display hex_digit_display_7 (.value(counter_2_q), .dp(1'b1));
  Hex_Digit_Display hex_digit_display_8 (.value(alu_1_alu_result[3:0]), .dp(1'b1));
  Hex_Digit_Display hex_digit_display_9 (.value(alu_1_alu_result[7:4]), .dp(1'b1));

  // Notes on the sheet:
  //   contents of rom_1 (hex, n*v repeats v):
  //   a ffffffff a 5 f0f0 f0f0 ffff0000 0 f ffffffff 1 fffffffe 5 ffffffff 1 5 1 80000000 80000000
  //   80000000 7fffffff 12345678
  //   contents of rom_2 (hex, n*v repeats v):
  //   14 1 14 5 ff0 ff0 ffff00 0 f0 1 ffffffff ffffffff 5 1 ffffffff 5 4 1 4 4 4 87654321
  //   contents of rom_3 (hex, n*v repeats v):
  //   0 0 1 1 2 3 4 a a 4*5 6 6 6 7 7 8 9 9 f
  //   contents of rom_4 (hex, n*v repeats v):
  //   1e 0 fffffff6 0 f0 fff0 ff00ff00 ffffffff ffffff00 1 0 1 0 0 1 0 10 0 8000000 f8000000 7ffffff
endmodule
