// Logisim project Branch_Compator.circ as structural Verilog: 1 circuit, main circuit main
module main (
  input  [31:0] Data_rs,
  input  [31:0] Data_rt,
  input  BrSel,
  output BranchTaken
);

  wire comparator_1_eq, not_1_out;

  Comparator #(.width(32)) comparator_1 (.a(Data_rs), .b(Data_rt), .eq(comparator_1_eq));  // open: gt, lt
  not not_1 (not_1_out, comparator_1_eq);
  Multiplexer multiplexer_1 (.in0(comparator_1_eq), .in1(not_1_out), .out(BranchTaken), .sel(BrSel), .en(1'b1));
endmodule
