// Logisim project Control.circ as structural Verilog: 1 circuit, main circuit main
module main (
  input  [5:0] opcode,
  input  [5:0] funct,
  output JumpSel,
  output Jump,
  output Branch,
  output LoadEx,
  output [1:0] MemRW,
  output [1:0] WdLen,
  output [1:0] WBSel,
  output [3:0] ALUSel,
  output BrSel,
  output [1:0] ImmSel,
  output [2:0] BSel,
  output [1:0] ASel,
  output [1:0] DestSel,
  output RegWEn
);

  wire [31:0] rom_1_data;

  ROM #(.addrWidth(12), .dataWidth(32)) rom_1 (
    .addr({opcode, funct}),
    .data({rom_1_data[31:27], RegWEn, DestSel, ASel, BSel, ImmSel, BrSel, ALUSel, WBSel, WdLen, rom_1_data[7], MemRW, LoadEx, Branch, Jump, JumpSel, rom_1_data[0]}));  // open: sel

  // Notes on the sheet:
  //   contents of rom_1 (hex, n*v repeats v):
  //   5d07700 3a0ff00 5d08700 5d09700 5d87700 3a0ff00 5d88700 5d89700 338ff06 538fb06 22*3a0ff00 5000700
  //   5000700 5001700 5001700 5002700 5003700 5004700 500a700 3a0ff00 3a0ff00 5005700 5006700 520b700
  //   83*3a0ff00 64*3b8ff04 64*6b8fb04 64*34e0f08 64*34f0f08 128*3a0ff00 128*4080700 64*4085700 64*4086700
  //   64*40a2700 64*40a3700 64*40a4700 64*48c0700 1024*3a0ff00 64*4080020 64*4080120 64*3a0ff00 64*4080220
  //   64*4080030 64*4080130 128*3a0ff00 64*3080c40 64*3080d40 64*3a0ff00 64*3080e40 1280*3a0ff00
endmodule
