// Logisim project Data_Memory.circ as structural Verilog: 2 circuits, main circuit main
module main (
  input  [31:0] Addr,
  input  [31:0] Data_rt,
  input  clk,
  input  LoadEx,
  input  [1:0] MemRW,
  input  [1:0] WdLen,
  output [31:0] Data_RD,
  output MisalignedAccessFlag
);

  wire and_1_out, and_2_out, \byte , half, load, none, not_1_out, not_2_out, not_3_out, not_4_out, or_1_out,
       or_2_out, or_3_out, RAM_load_en, RAM_store_en, store, word;
  wire [7:0] multiplexer_4_out;
  wire [15:0] multiplexer_5_out;
  wire [31:0] bit_extender_1_out, bit_extender_2_out, bit_extender_3_out, bit_extender_4_out,
       multiplexer_1_out, multiplexer_2_out, multiplexer_3_out, multiplexer_6_out, multiplexer_7_out,
       multiplexer_8_out, ReadWord;

  Multiplexer #(.select(2), .width(32)) multiplexer_1 (
    .in0({ReadWord[31:8], Data_rt[7:0]}), .in1({ReadWord[31:16], Data_rt[7:0], ReadWord[7:0]}),
    .in2({ReadWord[31:24], Data_rt[7:0], ReadWord[15:0]}), .in3({Data_rt[7:0], ReadWord[23:0]}),
    .out(multiplexer_1_out), .sel(Addr[1:0]), .en(1'b1));
  Multiplexer #(.width(32)) multiplexer_2 (
    .in0({ReadWord[31:16], Data_rt[15:0]}), .in1({Data_rt[15:0], ReadWord[15:0]}), .out(multiplexer_2_out),
    .sel(Addr[1]), .en(1'b1));
  Multiplexer #(.select(2), .width(32)) multiplexer_3 (
    .in0(multiplexer_1_out), .in1(multiplexer_2_out), .in2(Data_rt), .in3({32{1'b0}}),
    .out(multiplexer_3_out), .sel(WdLen), .en(1'b1));
  RAM #(.addrWidth(10), .dataWidth(32), .bus("separate")) ram_1 (
    .addr({Addr[9:2], 2'b00}), .din(multiplexer_3_out), .data(ReadWord), .str(RAM_store_en), .clk(clk),
    .ld(1'b1));  // open: sel, clr
  Multiplexer #(.select(2), .width(8)) multiplexer_4 (
    .in0(ReadWord[7:0]), .in1(ReadWord[15:8]), .in2(ReadWord[23:16]), .in3(ReadWord[31:24]),
    .out(multiplexer_4_out), .sel(Addr[1:0]), .en(1'b1));
  Multiplexer #(.width(16)) multiplexer_5 (
    .in0(ReadWord[15:0]), .in1(ReadWord[31:16]), .out(multiplexer_5_out), .sel(Addr[1]), .en(1'b1));
  Comparator #(.width(2)) comparator_1 (.a(MemRW), .b(2'b10), .eq(store));  // open: gt, lt
  Comparator #(.width(2)) comparator_2 (.a(MemRW), .b(2'b01), .eq(load));  // open: gt, lt
  Comparator #(.width(2)) comparator_3 (.a(WdLen), .b(2'b00), .eq(\byte ));  // open: gt, lt
  Comparator #(.width(2)) comparator_4 (.a(WdLen), .b(2'b01), .eq(half));  // open: gt, lt
  Comparator #(.width(2)) comparator_5 (.a(WdLen), .b(2'b10), .eq(word));  // open: gt, lt
  Comparator #(.width(2)) comparator_6 (.a(WdLen), .b(2'b11), .eq(none));  // open: gt, lt
  assign bit_extender_1_out = {{24{multiplexer_4_out[7]}}, multiplexer_4_out};  // Bit_Extender bit_extender_1
  Multiplexer #(.width(32)) multiplexer_6 (
    .in0(bit_extender_1_out), .in1(bit_extender_2_out), .out(multiplexer_6_out), .sel(LoadEx), .en(1'b1));
  assign bit_extender_2_out = {{24{1'b0}}, multiplexer_4_out};  // Bit_Extender bit_extender_2
  assign bit_extender_3_out = {{16{multiplexer_5_out[15]}}, multiplexer_5_out};  // Bit_Extender bit_extender_3
  Multiplexer #(.width(32)) multiplexer_7 (
    .in0(bit_extender_3_out), .in1(bit_extender_4_out), .out(multiplexer_7_out), .sel(LoadEx), .en(1'b1));
  assign bit_extender_4_out = {{16{1'b0}}, multiplexer_5_out};  // Bit_Extender bit_extender_4
  or or_1 (or_1_out, Addr[0], Addr[1]);
  and and_1 (and_1_out, or_1_out, \byte );
  and and_2 (and_2_out, Addr[0], half);
  not not_1 (not_1_out, MisalignedAccessFlag);
  not not_2 (not_2_out, none);
  not not_3 (not_3_out, MisalignedAccessFlag);
  not not_4 (not_4_out, none);
  Multiplexer #(.select(2), .width(32)) multiplexer_8 (
    .in0(multiplexer_6_out), .in1(multiplexer_7_out), .in2(ReadWord), .in3({32{1'b0}}),
    .out(multiplexer_8_out), .sel(WdLen), .en(1'b1));
  or or_2 (or_2_out, and_1_out, and_2_out);
  or or_3 (or_3_out, load, store);
  and and_3 (RAM_load_en, not_1_out, not_2_out, load);
  and and_4 (RAM_store_en, not_3_out, not_4_out, store);
  and and_5 (MisalignedAccessFlag, or_2_out, or_3_out);
  Multiplexer #(.width(32)) multiplexer_9 (
    .in0({32{1'b0}}), .in1(multiplexer_8_out), .out(Data_RD), .sel(RAM_load_en), .en(1'b1));

  // Other names for the same wires on the sheet: Data_rt_7_0[7:0] = Data_rt[7:0]; Data_rt_15_0[15:0] = Data_rt[15:0];
  //   ReadWord_15_0[15:0] = ReadWord[15:0]; ReadWord_23_0[23:0] = ReadWord[23:0];
  //   ReadWord_31_8[23:0] = ReadWord[31:8]; ReadWord_31_16[15:0] = ReadWord[31:16];
  //   ReadWord_31_24[7:0] = ReadWord[31:24]; ReadWord_7_0[7:0] = ReadWord[7:0]; lane[1:0] = Addr[1:0];
  //   lane_0 = Addr[0]; lane_1 = Addr[1]
endmodule

module DMEM_test (
);

  wire CLK, comparator_1_eq, main_1_misalignedaccessflag, not_1_out, not_2_out, rom_3_data, RST;
  wire [1:0] rom_4_data, rom_5_data;
  wire [3:0] counter_2_q, main_1_data_rd, main_1_data_rd_3;
  wire [7:0] counter_1_q;
  wire [31:0] rom_1_data, rom_2_data, rom_6_data;
  wire [31:4] main_1_data_rd_2;

  Counter #(.ongoal("stay")) counter_1 (.Q(counter_1_q), .clk(not_1_out));  // open: load, D, count, carry, clr
  not not_1 (not_1_out, CLK);
  Clock clock_1 (.out(CLK));
  ROM #(.dataWidth(32)) rom_1 (.addr(counter_1_q), .data(rom_1_data));  // open: sel
  ROM #(.dataWidth(32)) rom_2 (.addr(counter_1_q), .data(rom_2_data));  // open: sel
  ROM #(.dataWidth(1)) rom_3 (.addr(counter_1_q), .data(rom_3_data));  // open: sel
  ROM #(.dataWidth(2)) rom_4 (.addr(counter_1_q), .data(rom_4_data));  // open: sel
  ROM #(.dataWidth(2)) rom_5 (.addr(counter_1_q), .data(rom_5_data));  // open: sel
  ROM #(.dataWidth(32)) rom_6 (.addr(counter_1_q), .data(rom_6_data));  // open: sel
  main main_1 (
    .Addr(rom_1_data), .Data_rt(rom_2_data), .LoadEx(rom_3_data), .MemRW(rom_4_data), .WdLen(rom_5_data),
    .clk(CLK), .Data_RD({main_1_data_rd_2[31:16], main_1_data_rd_3, main_1_data_rd_2[11:4], main_1_data_rd}),
    .MisalignedAccessFlag(main_1_misalignedaccessflag));
  LED led_1 (.in(main_1_misalignedaccessflag));
  Comparator #(.width(32)) comparator_1 (
    .a({main_1_data_rd_2[31:16], main_1_data_rd_3, main_1_data_rd_2[11:4], main_1_data_rd}), .b(rom_6_data),
    .eq(comparator_1_eq));  // open: gt, lt
  Hex_Digit_Display hex_digit_display_1 (.value(main_1_data_rd_2[31:28]), .dp(1'b1));
  Hex_Digit_Display hex_digit_display_2 (.value(main_1_data_rd_2[27:24]), .dp(1'b1));
  not not_2 (not_2_out, comparator_1_eq);
  Hex_Digit_Display hex_digit_display_3 (.value(main_1_data_rd_2[23:20]), .dp(1'b1));
  Counter #(.width(4), .max('h5)) counter_2 (
    .count(not_2_out), .Q(counter_2_q), .clk(CLK), .clr(RST));  // open: load, D, carry
  Hex_Digit_Display hex_digit_display_4 (.value(main_1_data_rd_3), .dp(1'b1));
  Hex_Digit_Display hex_digit_display_5 (.value(main_1_data_rd_2[19:16]), .dp(1'b1));
  Hex_Digit_Display hex_digit_display_6 (.value(counter_2_q), .dp(1'b1));
  Hex_Digit_Display hex_digit_display_7 (.value(main_1_data_rd_2[11:8]), .dp(1'b1));
  Hex_Digit_Display hex_digit_display_8 (.value(main_1_data_rd), .dp(1'b1));
  Hex_Digit_Display hex_digit_display_9 (.value(main_1_data_rd_2[7:4]), .dp(1'b1));

  // Notes on the sheet:
  //   Addr_In
  //   Data_rt_In
  //   Load_Ex_In
  //   MemRW_In
  //   WdLen_In
  //   Data_RD_OUT
  //   contents of rom_1 (hex, n*v repeats v):
  //   9*0 9*1 9*2 9*3
  //   contents of rom_2 (hex, n*v repeats v):
  //   5*0 11 2233 44556677 6*0 11 2233 44556677 6*0 11 2233 44556677 6*0 11 2233 44556677
  //   contents of rom_3 (hex, n*v repeats v):
  //   0 1 0 1 6*0 1 0 1 6*0 1 0 1 6*0 1 0 1
  //   contents of rom_4 (hex, n*v repeats v):
  //   5*1 2 2 2 0 5*1 2 2 2 0 5*1 2 2 2 0 5*1 2 2 2
  //   contents of rom_5 (hex, n*v repeats v):
  //   0 0 1 1 2 0 1 2 3 0 0 1 1 2 0 1 2 3 0 0 1 1 2 0 1 2 3 0 0 1 1 2 0 1 2 3
  //   contents of rom_6 (hex, n*v repeats v):
  //   ffffffdd dd ffffccdd ccdd aabbccdd 4*0 ffffffcc cc 7*0 ffffffbb bb ffffaabb aabb 5*0 ffffffaa aa
endmodule
