// Logisim project Register_File.circ as structural Verilog: 3 circuits, main circuit Register_File
module Register_File (
  input  CLK,
  input  RESET,
  input  [31:0] Data_WR,
  input  [4:0] Addr_rs,
  input  [4:0] Addr_rt,
  input  [4:0] Addr_WR,
  input  RegWEn,
  output [31:0] Data_rs,
  output [31:0] Data_rt
);

  wire and_1_out, and_2_out, comparator_1_eq, comparator_2_eq, comparator_3_eq, EN__1, EN__2, EN__3, EN__4,
       EN__5, EN__6, EN__7, EN__8, EN__9, EN__10, EN__11, EN__12, EN__13, EN__14, EN__15, EN__16, EN__17,
       EN__18, EN__19, EN__20, EN__21, EN__22, EN__23, EN__24, EN__25, EN__26, EN__27, EN__28, EN__29,
       EN__30, EN__31, not_1_out;
  wire [4:0] multiplexer_1_out;
  wire [31:0] multiplexer_2_out, multiplexer_3_out, Q__1, Q__2, Q__3, Q__4, Q__5, Q__6, Q__7, Q__8, Q__9,
       Q__10, Q__11, Q__12, Q__13, Q__14, Q__15, Q__16, Q__17, Q__18, Q__19, Q__20, Q__21, Q__22, Q__23,
       Q__24, Q__25, Q__26, Q__27, Q__28, Q__29, Q__30, Q__31;

  Decoder #(.select(5)) decoder_1 (
    .out1(EN__1), .out2(EN__2), .out3(EN__3), .out4(EN__4), .out5(EN__5), .out6(EN__6), .out7(EN__7),
    .out8(EN__8), .out9(EN__9), .out10(EN__10), .out11(EN__11), .out12(EN__12), .out13(EN__13),
    .out14(EN__14), .out15(EN__15), .out16(EN__16), .out17(EN__17), .out18(EN__18), .out19(EN__19),
    .out20(EN__20), .out21(EN__21), .out22(EN__22), .out23(EN__23), .out24(EN__24), .out25(EN__25),
    .out26(EN__26), .out27(EN__27), .out28(EN__28), .out29(EN__29), .out30(EN__30), .out31(EN__31),
    .sel(multiplexer_1_out), .en(1'b1));  // open: out0
  Multiplexer #(.width(5)) multiplexer_1 (
    .in0({5{1'b0}}), .in1(Addr_WR), .out(multiplexer_1_out), .sel(RegWEn), .en(1'b1));
  Comparator #(.width(5)) comparator_1 (.a(multiplexer_1_out), .b({5{1'b0}}), .eq(comparator_1_eq));  // open: gt, lt
  Comparator #(.width(5)) comparator_2 (.a(Addr_rs), .b(multiplexer_1_out), .eq(comparator_2_eq));  // open: gt, lt
  Comparator #(.width(5)) comparator_3 (.a(Addr_rt), .b(multiplexer_1_out), .eq(comparator_3_eq));  // open: gt, lt
  not not_1 (not_1_out, comparator_1_eq);
  and and_1 (and_1_out, not_1_out, comparator_2_eq);
  and and_2 (and_2_out, not_1_out, comparator_3_eq);
  Register #(.width(32)) register_1 (.D(Data_WR), .en(EN__1), .Q(Q__1), .clk(CLK), .clr(RESET));
  Register #(.width(32)) register_2 (.D(Data_WR), .en(EN__2), .Q(Q__2), .clk(CLK), .clr(RESET));
  Register #(.width(32)) register_3 (.D(Data_WR), .en(EN__3), .Q(Q__3), .clk(CLK), .clr(RESET));
  Register #(.width(32)) register_4 (.D(Data_WR), .en(EN__4), .Q(Q__4), .clk(CLK), .clr(RESET));
  Register #(.width(32)) register_5 (.D(Data_WR), .en(EN__5), .Q(Q__5), .clk(CLK), .clr(RESET));
  Register #(.width(32)) register_6 (.D(Data_WR), .en(EN__6), .Q(Q__6), .clk(CLK), .clr(RESET));
  Register #(.width(32)) register_7 (.D(Data_WR), .en(EN__7), .Q(Q__7), .clk(CLK), .clr(RESET));
  Register #(.width(32)) register_8 (.D(Data_WR), .en(EN__8), .Q(Q__8), .clk(CLK), .clr(RESET));
  Register #(.width(32)) register_9 (.D(Data_WR), .en(EN__9), .Q(Q__9), .clk(CLK), .clr(RESET));
  Register #(.width(32)) register_10 (.D(Data_WR), .en(EN__10), .Q(Q__10), .clk(CLK), .clr(RESET));
  Register #(.width(32)) register_11 (.D(Data_WR), .en(EN__11), .Q(Q__11), .clk(CLK), .clr(RESET));
  Register #(.width(32)) register_12 (.D(Data_WR), .en(EN__12), .Q(Q__12), .clk(CLK), .clr(RESET));
  Register #(.width(32)) register_13 (.D(Data_WR), .en(EN__13), .Q(Q__13), .clk(CLK), .clr(RESET));
  Register #(.width(32)) register_14 (.D(Data_WR), .en(EN__14), .Q(Q__14), .clk(CLK), .clr(RESET));
  Register #(.width(32)) register_15 (.D(Data_WR), .en(EN__15), .Q(Q__15), .clk(CLK), .clr(RESET));
  Register #(.width(32)) register_16 (.D(Data_WR), .en(EN__16), .Q(Q__16), .clk(CLK), .clr(RESET));
  Register #(.width(32)) register_17 (.D(Data_WR), .en(EN__17), .Q(Q__17), .clk(CLK), .clr(RESET));
  Register #(.width(32)) register_18 (.D(Data_WR), .en(EN__18), .Q(Q__18), .clk(CLK), .clr(RESET));
  Register #(.width(32)) register_19 (.D(Data_WR), .en(EN__19), .Q(Q__19), .clk(CLK), .clr(RESET));
  Register #(.width(32)) register_20 (.D(Data_WR), .en(EN__20), .Q(Q__20), .clk(CLK), .clr(RESET));
  Register #(.width(32)) register_21 (.D(Data_WR), .en(EN__21), .Q(Q__21), .clk(CLK), .clr(RESET));
  Register #(.width(32)) register_22 (.D(Data_WR), .en(EN__22), .Q(Q__22), .clk(CLK), .clr(RESET));
  Register #(.width(32)) register_23 (.D(Data_WR), .en(EN__23), .Q(Q__23), .clk(CLK), .clr(RESET));
  Register #(.width(32)) register_24 (.D(Data_WR), .en(EN__24), .Q(Q__24), .clk(CLK), .clr(RESET));
  Register #(.width(32)) register_25 (.D(Data_WR), .en(EN__25), .Q(Q__25), .clk(CLK), .clr(RESET));
  Register #(.width(32)) register_26 (.D(Data_WR), .en(EN__26), .Q(Q__26), .clk(CLK), .clr(RESET));
  Register #(.width(32)) register_27 (.D(Data_WR), .en(EN__27), .Q(Q__27), .clk(CLK), .clr(RESET));
  Register #(.width(32)) register_28 (.D(Data_WR), .en(EN__28), .Q(Q__28), .clk(CLK), .clr(RESET));
  Register #(.width(32)) register_29 (.D(Data_WR), .en(EN__29), .Q(Q__29), .clk(CLK), .clr(RESET));
  Register #(.width(32)) register_30 (.D(Data_WR), .en(EN__30), .Q(Q__30), .clk(CLK), .clr(RESET));
  Register #(.width(32)) register_31 (.D(Data_WR), .en(EN__31), .Q(Q__31), .clk(CLK), .clr(RESET));
  Multiplexer #(.select(5), .width(32)) multiplexer_2 (
    .in0({32{1'b0}}), .in1(Q__1), .in2(Q__2), .in3(Q__3), .in4(Q__4), .in5(Q__5), .in6(Q__6), .in7(Q__7),
    .in8(Q__8), .in9(Q__9), .in10(Q__10), .in11(Q__11), .in12(Q__12), .in13(Q__13), .in14(Q__14),
    .in15(Q__15), .in16(Q__16), .in17(Q__17), .in18(Q__18), .in19(Q__19), .in20(Q__20), .in21(Q__21),
    .in22(Q__22), .in23(Q__23), .in24(Q__24), .in25(Q__25), .in26(Q__26), .in27(Q__27), .in28(Q__28),
    .in29(Q__29), .in30(Q__30), .in31(Q__31), .out(multiplexer_2_out), .sel(Addr_rs), .en(1'b1));
  Multiplexer #(.select(5), .width(32)) multiplexer_3 (
    .in0({32{1'b0}}), .in1(Q__1), .in2(Q__2), .in3(Q__3), .in4(Q__4), .in5(Q__5), .in6(Q__6), .in7(Q__7),
    .in8(Q__8), .in9(Q__9), .in10(Q__10), .in11(Q__11), .in12(Q__12), .in13(Q__13), .in14(Q__14),
    .in15(Q__15), .in16(Q__16), .in17(Q__17), .in18(Q__18), .in19(Q__19), .in20(Q__20), .in21(Q__21),
    .in22(Q__22), .in23(Q__23), .in24(Q__24), .in25(Q__25), .in26(Q__26), .in27(Q__27), .in28(Q__28),
    .in29(Q__29), .in30(Q__30), .in31(Q__31), .out(multiplexer_3_out), .sel(Addr_rt), .en(1'b1));
  Multiplexer #(.width(32)) multiplexer_4 (
    .in0(multiplexer_2_out), .in1(Data_WR), .out(Data_rs), .sel(and_1_out), .en(1'b1));
  Multiplexer #(.width(32)) multiplexer_5 (
    .in0(multiplexer_3_out), .in1(Data_WR), .out(Data_rt), .sel(and_2_out), .en(1'b1));

  // Other names for the same wires on the sheet: RST = RESET; WD[31:0] = Data_WR

  // Notes on the sheet:
  //   is Addr_WR_eff 0
  //   is Addr_WR_eff == Addr_rs
  //   is Addr_WR_eff == Addr_rt
  //   Bypass rs
  //   Bypass rt
endmodule

module REG_TEST (
);

  wire CLK, comparator_1_eq, comparator_2_eq, not_1_out, not_2_out, not_3_out, rom_2_data, RST;
  wire [3:0] counter_2_q, counter_3_q, register_file_1_data_rs_2, register_file_1_data_rt_2;
  wire [4:0] rom_3_data, rom_4_data, rom_5_data;
  wire [7:0] counter_1_q;
  wire [31:0] register_file_1_data_rs, register_file_1_data_rt, rom_1_data, rom_6_data, rom_7_data;

  Counter #(.ongoal("stay")) counter_1 (.Q(counter_1_q), .clk(not_1_out));  // open: load, D, count, carry, clr
  not not_1 (not_1_out, CLK);
  Clock clock_1 (.out(CLK));
  ROM #(.dataWidth(32)) rom_1 (.addr(counter_1_q), .data(rom_1_data));  // open: sel
  ROM #(.dataWidth(1)) rom_2 (.addr(counter_1_q), .data(rom_2_data));  // open: sel
  ROM #(.dataWidth(5)) rom_3 (.addr(counter_1_q), .data(rom_3_data));  // open: sel
  ROM #(.dataWidth(5)) rom_4 (.addr(counter_1_q), .data(rom_4_data));  // open: sel
  ROM #(.dataWidth(5)) rom_5 (.addr(counter_1_q), .data(rom_5_data));  // open: sel
  ROM #(.dataWidth(32)) rom_6 (.addr(counter_1_q), .data(rom_6_data));  // open: sel
  ROM #(.dataWidth(32)) rom_7 (.addr(counter_1_q), .data(rom_7_data));  // open: sel
  ROM #(.dataWidth(1)) rom_8 (.addr(counter_1_q), .data(RST));  // open: sel
  Register_File register_file_1 (
    .Data_WR(rom_1_data), .Addr_rs(rom_3_data), .Addr_rt(rom_4_data), .Addr_WR(rom_5_data), .CLK(CLK),
    .RESET(RST), .RegWEn(rom_2_data),
    .Data_rs({register_file_1_data_rs[31:16], register_file_1_data_rs_2, register_file_1_data_rs[11:0]}),
    .Data_rt({register_file_1_data_rt[31:16], register_file_1_data_rt_2, register_file_1_data_rt[11:0]}));
  Comparator #(.width(32)) comparator_1 (
    .a({register_file_1_data_rs[31:16], register_file_1_data_rs_2, register_file_1_data_rs[11:0]}),
    .b(rom_6_data), .eq(comparator_1_eq));  // open: gt, lt
  Comparator #(.width(32)) comparator_2 (
    .a({register_file_1_data_rt[31:16], register_file_1_data_rt_2, register_file_1_data_rt[11:0]}),
    .b(rom_7_data), .eq(comparator_2_eq));  // open: gt, lt
  Hex_Digit_Display hex_digit_display_1 (.value(register_file_1_data_rs[27:24]), .dp(1'b1));
  Hex_Digit_Display hex_digit_display_2 (.value(register_file_1_data_rs[31:28]), .dp(1'b1));
  Hex_Digit_Display hex_digit_display_3 (.value(register_file_1_data_rt[31:28]), .dp(1'b1));
  Hex_Digit_Display hex_digit_display_4 (.value(register_file_1_data_rt[27:24]), .dp(1'b1));
  not not_2 (not_2_out, comparator_1_eq);
  not not_3 (not_3_out, comparator_2_eq);
  Hex_Digit_Display hex_digit_display_5 (.value(register_file_1_data_rs[23:20]), .dp(1'b1));
  Hex_Digit_Display hex_digit_display_6 (.value(register_file_1_data_rt[23:20]), .dp(1'b1));
  Counter #(.width(4), .max('h5)) counter_2 (
    .count(not_2_out), .Q(counter_2_q), .clk(CLK), .clr(RST));  // open: load, D, carry
  Counter #(.width(4), .max('h5)) counter_3 (
    .count(not_3_out), .Q(counter_3_q), .clk(CLK), .clr(RST));  // open: load, D, carry
  Hex_Digit_Display hex_digit_display_7 (.value(register_file_1_data_rs[19:16]), .dp(1'b1));
  Hex_Digit_Display hex_digit_display_8 (.value(register_file_1_data_rs_2), .dp(1'b1));
  Hex_Digit_Display hex_digit_display_9 (.value(register_file_1_data_rt_2), .dp(1'b1));
  Hex_Digit_Display hex_digit_display_10 (.value(register_file_1_data_rt[19:16]), .dp(1'b1));
  Hex_Digit_Display hex_digit_display_11 (.value(counter_2_q), .dp(1'b1));
  Hex_Digit_Display hex_digit_display_12 (.value(counter_3_q), .dp(1'b1));
  Hex_Digit_Display hex_digit_display_13 (.value(register_file_1_data_rs[11:8]), .dp(1'b1));
  Hex_Digit_Display hex_digit_display_14 (.value(register_file_1_data_rt[11:8]), .dp(1'b1));
  Hex_Digit_Display hex_digit_display_15 (.value(register_file_1_data_rs[3:0]), .dp(1'b1));
  Hex_Digit_Display hex_digit_display_16 (.value(register_file_1_data_rs[7:4]), .dp(1'b1));
  Hex_Digit_Display hex_digit_display_17 (.value(register_file_1_data_rt[3:0]), .dp(1'b1));
  Hex_Digit_Display hex_digit_display_18 (.value(register_file_1_data_rt[7:4]), .dp(1'b1));

  // Notes on the sheet:
  //   Data_WR_IN
  //   RegWEN_IN
  //   Addr_rs_IN
  //   Addr_rt_IN
  //   Addr_WR_IN
  //   Data_rs_OUT
  //   Data_rt_OUT
  //   contents of rom_1 (hex, n*v repeats v):
  //   0 11111111 44444444 31313131 ffffffff 88888888
  //   contents of rom_2 (hex, n*v repeats v):
  //   0 4*1
  //   contents of rom_3 (hex, n*v repeats v):
  //   0 1 4 1f 0 8
  //   contents of rom_4 (hex, n*v repeats v):
  //   1 0 1 4 1f 1f
  //   contents of rom_5 (hex, n*v repeats v):
  //   0 1 4 1f
  //   contents of rom_6 (hex, n*v repeats v):
  //   0 11111111 44444444 31313131
  //   contents of rom_7 (hex, n*v repeats v):
  //   0 0 11111111 44444444 31313131 31313131
  //   contents of rom_8 (hex, n*v repeats v):
  //   1
endmodule

module REG_TEST_CONSTANT (
);

  wire button_2_out, CLK, RST;
  wire [3:0] register_file_1_data_rs, register_file_1_data_rs_3, register_file_1_data_rt_2;
  wire [31:0] register_file_1_data_rt;
  wire [31:4] register_file_1_data_rs_2;

  Button button_1 (.out(RST));
  Clock clock_1 (.out(CLK));
  Button button_2 (.out(button_2_out));
  Register_File register_file_1 (
    .Data_WR({32{1'b1}}), .Addr_rs(5'b00001), .Addr_rt(5'b00001), .Addr_WR(5'b00001), .CLK(CLK), .RESET(RST),
    .RegWEn(button_2_out),
    .Data_rs({register_file_1_data_rs_2[31:16], register_file_1_data_rs_3, register_file_1_data_rs_2[11:4], register_file_1_data_rs}),
    .Data_rt({register_file_1_data_rt[31:16], register_file_1_data_rt_2, register_file_1_data_rt[11:0]}));
  Hex_Digit_Display hex_digit_display_1 (.value(register_file_1_data_rs_2[27:24]), .dp(1'b1));
  Hex_Digit_Display hex_digit_display_2 (.value(register_file_1_data_rs_2[31:28]), .dp(1'b1));
  Hex_Digit_Display hex_digit_display_3 (.value(register_file_1_data_rt[31:28]), .dp(1'b1));
  Hex_Digit_Display hex_digit_display_4 (.value(register_file_1_data_rt[27:24]), .dp(1'b1));
  Hex_Digit_Display hex_digit_display_5 (.value(register_file_1_data_rs_2[23:20]), .dp(1'b1));
  Hex_Digit_Display hex_digit_display_6 (.value(register_file_1_data_rt[23:20]), .dp(1'b1));
  Hex_Digit_Display hex_digit_display_7 (.value(register_file_1_data_rs_2[19:16]), .dp(1'b1));
  Hex_Digit_Display hex_digit_display_8 (.value(register_file_1_data_rs_3), .dp(1'b1));
  Hex_Digit_Display hex_digit_display_9 (.value(register_file_1_data_rt[19:16]), .dp(1'b1));
  Hex_Digit_Display hex_digit_display_10 (.value(register_file_1_data_rt_2), .dp(1'b1));
  Hex_Digit_Display hex_digit_display_11 (.value(register_file_1_data_rs_2[11:8]), .dp(1'b1));
  Hex_Digit_Display hex_digit_display_12 (.value(register_file_1_data_rt[11:8]), .dp(1'b1));
  Hex_Digit_Display hex_digit_display_13 (.value(register_file_1_data_rs), .dp(1'b1));
  Hex_Digit_Display hex_digit_display_14 (.value(register_file_1_data_rs_2[7:4]), .dp(1'b1));
  Hex_Digit_Display hex_digit_display_15 (.value(register_file_1_data_rt[7:4]), .dp(1'b1));
  Hex_Digit_Display hex_digit_display_16 (.value(register_file_1_data_rt[3:0]), .dp(1'b1));
endmodule
