// Logisim project immediate_generator.circ as structural Verilog: 1 circuit, main circuit main
module main (
  input  [15:0] imm16,
  input  [2:0] ImmSel,
  output [31:0] ImmVal,
  output [31:0] BranchOff
);

  wire [31:0] bit_extender_1_out, bit_extender_2_out;

  assign bit_extender_1_out = {{16{imm16[15]}}, imm16};  // Bit_Extender bit_extender_1
  assign bit_extender_2_out = {{16{1'b0}}, imm16};  // Bit_Extender bit_extender_2
  Multiplexer #(.select(3), .width(32)) multiplexer_1 (
    .in0(bit_extender_1_out), .in1(bit_extender_2_out), .in2({imm16, {16{1'b0}}}), .out(ImmVal),
    .sel(ImmSel), .en(1'b1));  // open: in3, in4, in5, in6, in7
  Shifter #(.width(32)) shifter_1 (.in(bit_extender_1_out), .\dist (5'b00010), .out(BranchOff));
endmodule
