// Logisim project register_file_for_single.circ as structural Verilog: 1 circuit, main circuit main
module main (
  input  CLK,
  input  RESET,
  input  [31:0] Data_WR,
  input  [4:0] Addr_rs,
  input  [4:0] Addr_rt,
  input  [4:0] Addr_WR,
  input  RegWEn,
  output [31:0] Data_rs,
  output [31:0] Data_rt
);

  wire EN__1, EN__2, EN__3, EN__4, EN__5, EN__6, EN__7, EN__8, EN__9, EN__10, EN__11, EN__12, EN__13, EN__14,
       EN__15, EN__16, EN__17, EN__18, EN__19, EN__20, EN__21, EN__22, EN__23, EN__24, EN__25, EN__26,
       EN__27, EN__28, EN__29, EN__30, EN__31;
  wire [4:0] multiplexer_1_out;
  wire [31:0] Q__1, Q__2, Q__3, Q__4, Q__5, Q__6, Q__7, Q__8, Q__9, Q__10, Q__11, Q__12, Q__13, Q__14, Q__15,
       Q__16, Q__17, Q__18, Q__19, Q__20, Q__21, Q__22, Q__23, Q__24, Q__25, Q__26, Q__27, Q__28, Q__29,
       Q__30, Q__31;

  Decoder #(.select(5)) decoder_1 (
    .out1(EN__1), .out2(EN__2), .out3(EN__3), .out4(EN__4), .out5(EN__5), .out6(EN__6), .out7(EN__7),
    .out8(EN__8), .out9(EN__9), .out10(EN__10), .out11(EN__11), .out12(EN__12), .out13(EN__13),
    .out14(EN__14), .out15(EN__15), .out16(EN__16), .out17(EN__17), .out18(EN__18), .out19(EN__19),
    .out20(EN__20), .out21(EN__21), .out22(EN__22), .out23(EN__23), .out24(EN__24), .out25(EN__25),
    .out26(EN__26), .out27(EN__27), .out28(EN__28), .out29(EN__29), .out30(EN__30), .out31(EN__31),
    .sel(multiplexer_1_out), .en(1'b1));  // open: out0
  Multiplexer #(.width(5)) multiplexer_1 (
    .in0({5{1'b0}}), .in1(Addr_WR), .out(multiplexer_1_out), .sel(RegWEn), .en(1'b1));
  Register #(.width(32)) register_1 (.D(Data_WR), .en(EN__1), .Q(Q__1), .clk(CLK), .clr(RESET));
  Register #(.width(32)) register_2 (.D(Data_WR), .en(EN__2), .Q(Q__2), .clk(CLK), .clr(RESET));
  Register #(.width(32)) register_3 (.D(Data_WR), .en(EN__3), .Q(Q__3), .clk(CLK), .clr(RESET));
  Register #(.width(32)) register_4 (.D(Data_WR), .en(EN__4), .Q(Q__4), .clk(CLK), .clr(RESET));
  Register #(.width(32)) register_5 (.D(Data_WR), .en(EN__5), .Q(Q__5), .clk(CLK), .clr(RESET));
  Register #(.width(32)) register_6 (.D(Data_WR), .en(EN__6), .Q(Q__6), .clk(CLK), .clr(RESET));
  Register #(.width(32)) register_7 (.D(Data_WR), .en(EN__7), .Q(Q__7), .clk(CLK), .clr(RESET));
  Register #(.width(32)) register_8 (.D(Data_WR), .en(EN__8), .Q(Q__8), .clk(CLK), .clr(RESET));
  Register #(.width(32)) register_9 (.D(Data_WR), .en(EN__9), .Q(Q__9), .clk(CLK), .clr(RESET));
  Register #(.width(32)) register_10 (.D(Data_WR), .en(EN__10), .Q(Q__10), .clk(CLK), .clr(RESET));
  Register #(.width(32)) register_11 (.D(Data_WR), .en(EN__11), .Q(Q__11), .clk(CLK), .clr(RESET));
  Register #(.width(32)) register_12 (.D(Data_WR), .en(EN__12), .Q(Q__12), .clk(CLK), .clr(RESET));
  Register #(.width(32)) register_13 (.D(Data_WR), .en(EN__13), .Q(Q__13), .clk(CLK), .clr(RESET));
  Register #(.width(32)) register_14 (.D(Data_WR), .en(EN__14), .Q(Q__14), .clk(CLK), .clr(RESET));
  Register #(.width(32)) register_15 (.D(Data_WR), .en(EN__15), .Q(Q__15), .clk(CLK), .clr(RESET));
  Register #(.width(32)) register_16 (.D(Data_WR), .en(EN__16), .Q(Q__16), .clk(CLK), .clr(RESET));
  Register #(.width(32)) register_17 (.D(Data_WR), .en(EN__17), .Q(Q__17), .clk(CLK), .clr(RESET));
  Register #(.width(32)) register_18 (.D(Data_WR), .en(EN__18), .Q(Q__18), .clk(CLK), .clr(RESET));
  Register #(.width(32)) register_19 (.D(Data_WR), .en(EN__19), .Q(Q__19), .clk(CLK), .clr(RESET));
  Register #(.width(32)) register_20 (.D(Data_WR), .en(EN__20), .Q(Q__20), .clk(CLK), .clr(RESET));
  Register #(.width(32)) register_21 (.D(Data_WR), .en(EN__21), .Q(Q__21), .clk(CLK), .clr(RESET));
  Register #(.width(32)) register_22 (.D(Data_WR), .en(EN__22), .Q(Q__22), .clk(CLK), .clr(RESET));
  Register #(.width(32)) register_23 (.D(Data_WR), .en(EN__23), .Q(Q__23), .clk(CLK), .clr(RESET));
  Register #(.width(32)) register_24 (.D(Data_WR), .en(EN__24), .Q(Q__24), .clk(CLK), .clr(RESET));
  Register #(.width(32)) register_25 (.D(Data_WR), .en(EN__25), .Q(Q__25), .clk(CLK), .clr(RESET));
  Register #(.width(32)) register_26 (.D(Data_WR), .en(EN__26), .Q(Q__26), .clk(CLK), .clr(RESET));
  Register #(.width(32)) register_27 (.D(Data_WR), .en(EN__27), .Q(Q__27), .clk(CLK), .clr(RESET));
  Register #(.width(32)) register_28 (.D(Data_WR), .en(EN__28), .Q(Q__28), .clk(CLK), .clr(RESET));
  Register #(.width(32)) register_29 (.D(Data_WR), .en(EN__29), .Q(Q__29), .clk(CLK), .clr(RESET));
  Register #(.width(32)) register_30 (.D(Data_WR), .en(EN__30), .Q(Q__30), .clk(CLK), .clr(RESET));
  Register #(.width(32)) register_31 (.D(Data_WR), .en(EN__31), .Q(Q__31), .clk(CLK), .clr(RESET));
  Multiplexer #(.select(5), .width(32)) multiplexer_2 (
    .in0({32{1'b0}}), .in1(Q__1), .in2(Q__2), .in3(Q__3), .in4(Q__4), .in5(Q__5), .in6(Q__6), .in7(Q__7),
    .in8(Q__8), .in9(Q__9), .in10(Q__10), .in11(Q__11), .in12(Q__12), .in13(Q__13), .in14(Q__14),
    .in15(Q__15), .in16(Q__16), .in17(Q__17), .in18(Q__18), .in19(Q__19), .in20(Q__20), .in21(Q__21),
    .in22(Q__22), .in23(Q__23), .in24(Q__24), .in25(Q__25), .in26(Q__26), .in27(Q__27), .in28(Q__28),
    .in29(Q__29), .in30(Q__30), .in31(Q__31), .out(Data_rs), .sel(Addr_rs), .en(1'b1));
  Multiplexer #(.select(5), .width(32)) multiplexer_3 (
    .in0({32{1'b0}}), .in1(Q__1), .in2(Q__2), .in3(Q__3), .in4(Q__4), .in5(Q__5), .in6(Q__6), .in7(Q__7),
    .in8(Q__8), .in9(Q__9), .in10(Q__10), .in11(Q__11), .in12(Q__12), .in13(Q__13), .in14(Q__14),
    .in15(Q__15), .in16(Q__16), .in17(Q__17), .in18(Q__18), .in19(Q__19), .in20(Q__20), .in21(Q__21),
    .in22(Q__22), .in23(Q__23), .in24(Q__24), .in25(Q__25), .in26(Q__26), .in27(Q__27), .in28(Q__28),
    .in29(Q__29), .in30(Q__30), .in31(Q__31), .out(Data_rt), .sel(Addr_rt), .en(1'b1));

  // Other names for the same wires on the sheet: RST = RESET; WD[31:0] = Data_WR
endmodule
