// Logisim project jump_target_generator.circ as structural Verilog: 1 circuit, main circuit main
module main (
  input  [25:0] target26,
  input  [31:0] JumpImmTarget,
  input  [31:0] PCPlus4
);


  assign PCPlus4[31:28] = JumpImmTarget[31:28];
  assign target26 = JumpImmTarget[27:2];
  // also tied to GND on the sheet: {JumpImmTarget[0], JumpImmTarget[1], PCPlus4[0], PCPlus4[1], PCPlus4[2], PCPlus4[3], PCPlus4[4], PCPlus4[5], PCPlus4[6], PCPlus4[7], PCPlus4[8], PCPlus4[9], PCPlus4[10], PCPlus4[11], PCPlus4[12], PCPlus4[13], PCPlus4[14], PCPlus4[15], PCPlus4[16], PCPlus4[17], PCPlus4[18], PCPlus4[19], PCPlus4[20], PCPlus4[21], PCPlus4[22], PCPlus4[23], PCPlus4[24], PCPlus4[25], PCPlus4[26], PCPlus4[27]}
endmodule
