// Logisim project pc_control.circ as structural Verilog: 1 circuit, main circuit main
module main (
  input  Jump,
  input  Branch,
  input  BranchTaken,
  output [1:0] out_4
);

  wire and_1_out;
  wire [1:0] multiplexer_1_out;

  and and_1 (and_1_out, Branch, BranchTaken);
  Multiplexer #(.width(2)) multiplexer_1 (
    .in0(2'b00), .in1(2'b01), .out(multiplexer_1_out), .sel(and_1_out), .en(1'b1));
  Multiplexer #(.width(2)) multiplexer_2 (.in0(multiplexer_1_out), .in1(2'b10), .out(out_4), .sel(Jump), .en(1'b1));
endmodule
